# Fritzing sketch cute little shit prfboard layout (saved by Fritzing 0.9.3b)
perfboards: 1

parts:
  U1 = atmega328 [package=dip]
  IC1 = Voltage Regulator [package=78xxl]
  Part1 = Logic Level Converter  # not connected
  Part2 = Bluetooth HC-05 Macho  # not connected
  J1 = Piezo Speaker
  XTAL1 = Crystal [frequency="16 Mhz" package=SMD]  # not connected
  C1 = Capacitor [package=cap-pth-small2]
  C3 = Electrolytic Capacitor [capacitance=10μF package="0605 [SMD, electrolytic]"]
  R1 = Resistor [tolerance=±5% resistance=220 package="0805 [SMD]"]  # not connected
  LED1 = LED - 3mm [color="Green (555nm)" package="3 mm [THT]"]  # not connected
  S1 = Momentary Switch [package=ksa_sealed_tac_switch]  # not connected
  IC2 = IC, DIP package, 16 pins [chip_label=IC]
  C4 = Electrolytic Capacitor [capacitance=10μF package="0605 [SMD, electrolytic]"]
  R2 = Resistor [tolerance=±5% resistance=220 package="0805 [SMD]"]  # not connected
  C5 = Capacitor [package=cap-pth-small2]  # not connected
  C6 = Capacitor [package=cap-pth-small2]  # not connected
  LED2 = LED - 3mm [color="Red (633nm)" package="3 mm [THT]"]
  R3 = Resistor [tolerance=±5% resistance=220 package="0805 [SMD]"]
  S2 = Taiway 100-SP-X-T1 SPDT Miniature Toggle Switch [part_number=100-SP-X-T1-0-0-B1-M2 package=THT]  # not connected
  VCC1 = Battery block 9V
  R4 = Resistor [tolerance=±5% resistance=220 package="0805 [SMD]"]  # not connected
  R5 = Resistor [tolerance=±5% resistance=220 package="0805 [SMD]"]  # not connected
  D1 = Zener Diode [part_number=1N4732A breakdown_voltage=3.6V package="300 mil [THT]"]  # not connected
  JP1 = Header 6 [package=1x06_smd_straight_alt]
  M1 = DC Motor  # not connected
  M2 = DC Motor  # not connected

nets:
  N1: U1.D10_(PWM), JP1.2
  N2: U1.D13, C1.2
  N3: U1.A1, IC2.pin16
  N4: U1.A3, JP1.6
  N5: IC1.GND, VCC1.-
  N6: J1.pin1, C3.-, C4.-
  N7: LED2.cathode, R3.Pin_0
